# Fritzing sketch KeyboardInstrument (saved by Fritzing 0.9.3b)
breadboards: 1

parts:
  U1 = ATTINY45 [package=dip]
  S1 = Pushbutton [package="[THT]"]  # not connected
  S2 = Pushbutton [package="[THT]"]  # not connected
  S3 = Pushbutton [package="[THT]"]  # not connected
  S4 = Pushbutton [package="[THT]"]  # not connected
  J1 = Piezo Speaker
  R1 = Resistor [tolerance=±5% resistance=220 package=THT]
  R2 = Resistor [tolerance=±5% resistance=10k package=THT]
  R3 = Resistor [tolerance=±5% resistance=1M package=THT]
  R4 = Resistor [tolerance=±5% resistance=10k package=THT]

nets:
  N1: U1.PB4(ADC2), R4.Pin_0
  N2: U1.GND, J1.pin1, R1.Pin_1, R2.Pin_1, R3.Pin_1, R4.Pin_1
