# Fritzing sketch DripClock (saved by Fritzing 0.9.3b)
breadboards: 1

parts:
  Part1 = Adafruit Trinket 5V
  Part2 = Adafruit DS1307 RTC Breakout [part_number="Adafruit #264"]
  NEOPIXEL1 = Neopixel Strip -- Black (60/m)
  S1 = Pushbutton [package="[THT]"]
  R1 = Resistor [tolerance=±5% resistance=10k package=THT]

nets:
  GND: Part1.GND, Part2.GND, NEOPIXEL1.GND, R1.Pin_0
  N1: Part1.#1, S1.Pin_3, S1.Pin_4, R1.Pin_1
  N2: Part1.#2, Part2.SCL
  N3: Part1.#0, Part2.SDA
  VCC: Part1.VBUS, Part2.VCC, NEOPIXEL1.+5V, S1.Pin_1, S1.Pin_2
  N4: Part1.#4, NEOPIXEL1.DI

custom parts:
  Adafruit Trinket 5V: Trinket may be small, but do not be fooled by its size! It's a tiny microcontroller board, built around the Atmel ATtiny85, a little chip with a lot of power. We wanted to design a microcontroller board that was small enough to fit into any project, and low cost enough to use without hesitation. Perfect for when you don't want to give up your expensive dev-board and you aren't willing to take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
  Adafruit DS1307 RTC Breakout: This is a great battery-backed real time clock (RTC) that allows your microcontroller project to keep track of time even if it is reprogrammed, or if the power is lost. Perfect for datalogging, clock-building, time stamping, timers and alarms, etc. The DS1307 is the most popular RTC - but it requires 5V power to work (although we've used it with 5V power and 3.3V logic successfully) PCB &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
  Neopixel Strip -- Black (60/m): Neopixel Strip, Black, 60 pixels per meter.
