# Fritzing sketch legocar_perfboard_2 (saved by Fritzing 0.9.3b)
circuit board: 8.46667cm x 5.64444cm
stripboards: 1

parts:
  U6 = attiny85 [package=dip]
  J5 = Piezo Speaker
  IC5 = Voltage Regulator [package=to-220-alt]
  VCC2 = Battery block 9V
  IC6 = H-Bridge [package=THT]
  M3 = DC Motor
  J6 = Basic Servo
  U7 = atmega168 [package=dip]
  C7 = Capacitor Polarized [package=cpol-radial-100uf-25v]
  U8 = XD-RF-5V [package=THT]
  Y3 = CRYSTAL [package=crystal-smd-10.5x4.8-2pin]
  C8 = Capacitor [package=cap-pth-small2]
  C9 = Capacitor [package=cap-pth-small2]

nets:
  N1: U6.Pin_3, U7.D5_(PWM)
  GND1: U6.Pin_4, J5.pin1, IC5.IN, VCC2.-, IC6.GND1, IC6.GND2
  N2: U6.Pin_6, J5.pin2
  VCC: U6.Pin_8, IC5.OUT, IC6.VCC1, J6.vcc, U7.VCC, U7.AVCC, U7.AREF, C7.-
  N3: IC5.GND, VCC2.+, IC6.VCC2
  N4: IC6.1_2EN, U7.D6_(PWM)
  N5: IC6.1A, U7.D3_(PWM)
  N6: IC6.1Y, M3.pin_1
  N7: IC6.2Y, M3.pin_2
  N8: IC6.2A, U7.D2
  N9: J6.pulse, U7.D9_(PWM)
  N10: U7.GND#7, U8.GND
  N11: U7.XLAT1, Y3.1, C8.1
  N12: U7.XLAT2, Y3.2, C9.2
  N13: U7.D11_(PWM), U8.DATA
  N14: U7.GND#21, C7.+
  N15: C8.2, C9.1

custom parts:
  XD-RF-5V: This is 433Mhz RF transmitter with receiver kit for Arduino ARM MCU wireless Application environment: Remote control switch, receiver module, motorcycles, automobile anti-theft products, home security products, electric doors, shutter doors, windows, remote control socket, remote control LED, remote audio remote control electric doors, garage door remote control, remote control retractable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
